# Fritzing sketch autodraha (saved by Fritzing 0.9.2b)
breadboards: 1

parts:
  Part2 = SRF05 Ultrasonic Rangefinder
  Part3 = SRF05 Ultrasonic Rangefinder
  Part4 = KY-008 Laser Transmitter Module [package="Breakout board"]
  Part5 = Arduino Uno (Rev3)
  D1 = SOLAR-IXYS [package=solarbit-12x1]
  Nokia_5110_LCD_Module1 = Nokia 5110 LCD
  R1 = Resistor [tolerance=±5% resistance=15k package=THT]

nets:
  VCC: Part2.VCC, Part3.VCC, Part5.5V
  N1: Part2.Trig, Part5.D3_PWM
  N2: Part2.Echo, Part5.D2
  GND: Part2.GND, Part3.GND, Part4.-, Part5.GND, D1.C, Nokia_5110_LCD_Module1.GND_(out), Nokia_5110_LCD_Module1.LED_(out), R1.Pin_1
  N3: Part3.Trig, Part5.D5_PWM
  N4: Part3.Echo, Part5.D4
  N5: Part4.S, Part5.D8
  N6: Part5.A1, Nokia_5110_LCD_Module1.SCE, Nokia_5110_LCD_Module1.SCE_(out)
  N7: Part5.A2, Nokia_5110_LCD_Module1.RST, Nokia_5110_LCD_Module1.RST_(out)
  N8: Part5.A3, Nokia_5110_LCD_Module1.D/C, Nokia_5110_LCD_Module1.D/C_(out)
  N9: Part5.A4/SDA, Nokia_5110_LCD_Module1.DN(MOSI), Nokia_5110_LCD_Module1.DN(MODI)_(out)
  N10: Part5.A5/SCL, Nokia_5110_LCD_Module1.SCLK_(out)
  N11: Part5.D9_PWM, D1.A, R1.Pin_0
  N12: Part5.3V3, Nokia_5110_LCD_Module1.VCC_(out)

custom parts:
  KY-008 Laser Transmitter Module: Laser Transmitter module KY-008 for Arduino, emits a dot shaped red laser beam.
  Nokia 5110 LCD: Nokia 5110 Graphic 84*48 LCD module such as the Sparkfun LCD-10168 or the clones from Ebay. There is example code for the Arduino available from the Sparkfun site in https://learn.sparkfun.com/tutorials/graphic-lcd-hookup-guide This is a 3.3V device, if you are running it from a 5V micro you need a 5V tolorant level translator such as the 74ahc367 to protect the signal imputs. Rafa G. did a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
